# Fritzing sketch Solar-Node-HW-0.0.2 (saved by Fritzing 0.9.10b)
breadboards: 1

parts:
  Mod1 = Amica NodeMCU DEVKIT 1.0
  Part1 = INA219 High Side DC Current Sensor Breakout [part_number=904]
  OLED_I2C1 = OLED 128x64 I2C Monochrome Display
  A1 = Solar power manger 5V
  Bat1 = battery_holder_single_18650
  Bat2 = battery_holder_single_18650
  PIR1 = PIR sensor

nets:
  N1: Mod1.pin1, Mod1.pin_10, Mod1.pin_26
  GND: Mod1.pin2, Mod1.pin_9, Mod1.pin_25, Mod1.pin_29, Part1.GND, OLED_I2C1.GND, A1.Pin_1, A1.Pin_4, A1.Pin_7, Bat2.+#0, PIR1.GND
  N2: Mod1.pin6, PIR1.SIG
  N3: Mod1.pin_13, Part1.SDA, OLED_I2C1.SDA
  N4: Mod1.pin_14, Part1.SCL, OLED_I2C1.SCK
  VCC: Mod1.pin_30, Part1.VCC, OLED_I2C1.VDD
  N5: Part1.VIN-, A1.Pin_2
  N6: Part1.VIN+, Bat1.+, Bat2.+#1
  N7: A1.Pin_9, PIR1.VDD
  N8: A1.Pin_11, A1.Pin_12

custom parts:
  INA219 High Side DC Current Sensor Breakout: This breakout board will solve all your power-monitoring problems. Instead of struggling with two multimeters, you can just use the handy INA219B chip on this breakout to both measure both the high side voltage and DC current draw over I2C with 1% precision. Most current-measuring devices such as our current panel meter are only good for low side measuring. That means that unless you want to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
  Solar power manger 5V: Solar Power Manager 5V is a small power and high-efficiency solar power management module designed for 5V solar panel.
  battery_holder_single_18650: single 18650 battery holder
